# Fritzing sketch LP_DLP_Schematic (saved by Fritzing 0.8.7b)

parts:
  Launchpad1 = TI Launchpad MSP430G2
  I2C_J17 = female pin header, 4 pins [form="♀ (female)"]
  Trigger_J17 = female pin header, 6 pins [form="♀ (female)"]

nets:
  N1: Launchpad1.p10, Trigger_J17.pin1
  N2: Launchpad1.p14, I2C_J17.pin1
  N3: Launchpad1.p15, I2C_J17.pin2
  N4: Launchpad1.p20, Trigger_J17.pin3

notes:
  SDA
  SCL
  GND
  DLP J17 I2C1
  DLP J11 Trigger Input
  Trigger 1
